# Fritzing sketch connection (saved by Fritzing 0.9.3b)
breadboards: 1

parts:
  Raspberry_Pi_Zero1 = Raspberry Pi Zero
  IC1 = MCP3008 8-channel 10-bit ADC [part_number=MCP3008]
  Parça1 = Thumb Joystick
  Parça2 = Thumb Joystick
  S1 = Pushbutton [package="[THT]"]
  S2 = Pushbutton [package="[THT]"]
  S3 = Pushbutton [package="[THT]"]
  S4 = Pushbutton [package="[THT]"]

nets:
  VCC: Raspberry_Pi_Zero1.3V3, IC1.no_name_yet#15, IC1.no_name_yet#16, Parça1.VCC, Parça2.VCC
  N1: Raspberry_Pi_Zero1.GPIO10, IC1.no_name_yet#11
  N2: Raspberry_Pi_Zero1.GPIO9, IC1.no_name_yet#12
  N3: Raspberry_Pi_Zero1.GPIO11, IC1.no_name_yet#13
  N4: Raspberry_Pi_Zero1.GPIO12, S4.Pin_4
  N5: Raspberry_Pi_Zero1.GPIO8, IC1.no_name_yet#10
  N6: Raspberry_Pi_Zero1.GPIO25, S3.Pin_4
  N7: Raspberry_Pi_Zero1.GPIO24, S2.Pin_4
  N8: Raspberry_Pi_Zero1.GPIO23, S1.Pin_4
  GND: Raspberry_Pi_Zero1.GND, IC1.no_name_yet#9, IC1.no_name_yet#14, Parça1.GND, Parça2.GND, S1.Pin_2, S2.Pin_2, S3.Pin_1, S3.Pin_2, S4.Pin_1, S4.Pin_2
  N9: IC1.no_name_yet#1, Parça1.HORZ
  N10: IC1.no_name_yet#2, Parça1.VERT
  N11: IC1.no_name_yet#7, Parça2.HORZ
  N12: IC1.no_name_yet#8, Parça2.VERT

notes:
  Uçak modu seçimi
  Arm/disarm fonksiyonu
  Sağ kumanda kolu
  Sol kumanda kolu
