# Fritzing sketch connection (saved by Fritzing 0.9.3b)
breadboards: 1

parts:
  Raspberry_Pi_Zero1 = Raspberry Pi Zero
  IC1 = MCP3008 8-channel 10-bit ADC [part_number=MCP3008]
  Parça1 = Thumb Joystick
  Parça2 = Thumb Joystick
  S1 = Pushbutton [package="[SMD]"]
  S2 = Pushbutton [package="[SMD]"]
  S3 = Pushbutton [package="[SMD]"]
  S4 = Pushbutton [package="[SMD]"]

nets:
  VCC: Raspberry_Pi_Zero1.3v3, IC1.no_name_yet#15, IC1.no_name_yet#16, Parça1.VCC, Parça2.VCC
  N1: Raspberry_Pi_Zero1.GPIO2, S1.Pin_3, S1.Pin_4
  N2: Raspberry_Pi_Zero1.GPIO3, S3.Pin_3, S3.Pin_4
  N3: Raspberry_Pi_Zero1.GPIO4, S2.Pin_3, S2.Pin_4
  N4: Raspberry_Pi_Zero1.GPIO17, S4.Pin_1, S4.Pin_2
  N5: Raspberry_Pi_Zero1.GPIO13, IC1.no_name_yet#11
  N6: Raspberry_Pi_Zero1.GPIO19, IC1.no_name_yet#12
  N7: Raspberry_Pi_Zero1.GPIO26, IC1.no_name_yet#13
  N8: Raspberry_Pi_Zero1.GPIO20, IC1.no_name_yet#10
  GND: Raspberry_Pi_Zero1.GND, IC1.no_name_yet#9, IC1.no_name_yet#14, Parça1.GND, Parça2.GND, S1.Pin_1, S2.Pin_1, S2.Pin_2, S3.Pin_1, S3.Pin_2, S4.Pin_3, S4.Pin_4
  N9: IC1.no_name_yet#1, Parça2.HORZ
  N10: IC1.no_name_yet#2, Parça2.VERT
  N11: IC1.no_name_yet#7, Parça1.SEL, Parça1.HORZ
  N12: IC1.no_name_yet#8, Parça1.VERT
